# Fritzing sketch button_box (saved by Fritzing 0.9.4)

parts:
  Bauteil1 = Arduino Uno (Rev3) - ICSP
  S1 = Toggle Switch spst [package=THT]
  S2 = Toggle Switch spst [package=THT]
  BUTTON1 = Arcade Button (red)
  BUTTON1_2 = Arcade Button (red)
  BUTTON2 = Arcade Button (red)
  BUTTON3 = Arcade Button (blue)
  BUTTON4 = Arcade Button (blue)
  BUTTON5 = Arcade Button (blue)
  R1 = Resistor [tolerance=±5% resistance=10k package="1206 [SMD]"]
  R2 = Resistor [tolerance=±5% resistance=10k package="1206 [SMD]"]
  R3 = Resistor [tolerance=±5% resistance=10k package="1206 [SMD]"]
  D1 = Diode [package=diode-1n4148]
  D2 = Diode [package=diode-1n4148]
  D3 = Diode [package=diode-1n4148]
  D4 = Diode [package=diode-1n4148]
  D5 = Diode [package=diode-1n4148]
  D6 = Diode [package=diode-1n4148]
  D7 = Diode [package=diode-1n4148]
  D8 = Diode [package=diode-1n4148]
  LED1 = LED - 5mm [color="Red (633nm)" package="5 mm [THT]"]
  J1 = Piezo Speaker
  LED2 = LED - 5mm [color="Red (633nm)" package="5 mm [THT]"]
  LED3 = LED - 5mm [color="Red (633nm)" package="5 mm [THT]"]
  LED4 = LED - 5mm [color="Blue (525nm)" package="5 mm [THT]"]
  LED5 = LED - 5mm [color="Blue (525nm)" package="5 mm [THT]"]
  LED6 = LED - 5mm [color="Blue (525nm)" package="5 mm [THT]"]
  LED7 = LED - 5mm [color="Red (633nm)" part_number="internally connected" package="5 mm [THT]"]
  LED8 = LED - 5mm [color="Blue (525nm)" part_number=not_enough_gpio package="5 mm [THT]"]
  VCC1 = 4 x AAA Battery Mount
  S3 = Toggle Switch spst [package=THT]
  Bauteil2 = 0.56" 7-segment LED Backpack [part_number=879]
  C1 = Capacitor Polarized [part_number=1000uF package=panasonic_e]
  R4 = Resistor [tolerance=±5% resistance=1k package="1206 [SMD]"]
  R5 = Resistor [tolerance=±5% resistance=1k package="1206 [SMD]"]
  Bauteil4 = PowerBoost 1000 Basic [part_number="Pololu U1V11F5"]
  Q1 = npn-Powertransistor [part_number="BC 548C" package="TO220 [THT]"]
  Q2 = npn-Powertransistor [part_number="BC 548C" package="TO220 [THT]"]
  Q3 = npn-Powertransistor [part_number="BC 548C" package="TO220 [THT]"]
  R6 = Resistor [tolerance=±5% resistance=1k package=THT]
  R7 = Resistor [tolerance=±5% resistance=1k package=THT]
  R8 = Resistor [tolerance=±5% resistance=1k package=THT]
  R9 = Resistor [tolerance=±5% resistance=100 package=THT]
  R10 = Resistor [tolerance=±5% resistance=100 package=THT]
  R11 = Resistor [tolerance=±5% resistance=100 package=THT]
  JOY1 = Adafruit Arcade Joystick
  Bauteil3 = 16 NeoPixel Ring [part_number=1463]
  R12 = Resistor [tolerance=±5% resistance=100 package=THT]

nets:
  N1: Bauteil1.A0, JOY1.N
  N2: Bauteil1.A1, JOY1.S
  N3: Bauteil1.A2, JOY1.W
  N4: Bauteil1.A3, JOY1.E
  N5: Bauteil1.A5/SCL, Bauteil2.SCL
  N6: Bauteil1.ICSP_MISO, Bauteil1.D12/MISO, D4.C, D5.C, D6.C
  5V: Bauteil1.5V, R1.Pin_0, R2.Pin_0, R3.Pin_0, Bauteil2.VDD, C1.+, Bauteil4.5.0V, R9.Pin_0, R10.Pin_0, R11.Pin_0, Bauteil3.VDD
  N7: Bauteil1.ICSP_SCK, Bauteil1.D13/SCK, LED7.anode, LED8.anode
  N8: Bauteil1.ICSP_MOSI, Bauteil1.D11_PWM/MOSI, D1.C, D2.C, D3.C
  GND: Bauteil1.GND, J1.pin2, VCC1.-, Bauteil2.GND, C1.-, Bauteil4.GND, JOY1.COM, Bauteil3.GND
  N9: Bauteil1.D8, S2.COM, BUTTON1_2.no_name_yet#1, BUTTON4.no_name_yet#1, R2.Pin_1
  N10: Bauteil1.D9_PWM, BUTTON1.no_name_yet#1, BUTTON5.no_name_yet#1, R3.Pin_1
  N11: Bauteil1.D10_PWM/SS, D7.C, D8.C
  N12: Bauteil1.A4/SDA, Bauteil2.SDA
  N13: Bauteil1.D0/RX, R12.Pin_1
  N14: Bauteil1.D1/TX, R4.Pin_0, R5.Pin_0
  N15: Bauteil1.D2, R8.Pin_0
  N16: Bauteil1.D3_PWM, R7.Pin_0
  N17: Bauteil1.D4, R6.Pin_0
  N18: Bauteil1.D5_PWM, LED4.cathode, LED5.cathode, LED6.cathode
  N19: Bauteil1.D6_PWM, LED1.cathode, LED2.cathode, LED3.cathode
  N20: Bauteil1.D7, S1.COM, BUTTON2.no_name_yet#1, BUTTON3.no_name_yet#1, R1.Pin_1
  N21: S1.L1, D7.A, LED8.cathode
  N22: S2.L1, D8.A, LED7.cathode
  N23: BUTTON1.no_name_yet#2, D4.A
  N24: BUTTON1_2.no_name_yet#2, D5.A
  N25: BUTTON2.no_name_yet#2, D6.A
  N26: BUTTON3.no_name_yet#2, D2.A
  N27: BUTTON4.no_name_yet#2, D3.A
  N28: BUTTON5.no_name_yet#2, D1.A
  N29: LED1.anode, LED4.anode, Q1.emitter
  N30: J1.pin1, R12.Pin_0
  N31: LED2.anode, LED5.anode, Q2.emitter
  N32: LED3.anode, LED6.anode, Q3.emitter
  N33: VCC1.+, S3.COM
  N34: S3.L1, Bauteil4.VBAT
  N35: R4.Pin_1, R5.Pin_1, Bauteil3.IN
  N36: Q1.base, R8.Pin_1
  N37: Q1.collector, R11.Pin_1
  N38: Q2.base, R7.Pin_1
  N39: Q2.collector, R10.Pin_1
  N40: Q3.base, R6.Pin_1
  N41: Q3.collector, R9.Pin_1

custom parts:
  Toggle Switch spst: Toggle Switch single pole single throw
  Arcade Button (red): Adafruit Arcade Button (red)
  Arcade Button (blue): Adafruit Arcade Button (blue)
  0.56" 7-segment LED Backpack: This 0.56" 7-segment LED display includes a driver chip for simple control via an I2C interface. The backpack features address-selection jumpers so you can connect up to eight displays on a single I2C bus.
  PowerBoost 1000 Basic: The PowerBoost 1000 is a little DC/DC boost converter module that can run from 1.8V batteries or higher, and convert the battery output to 5.2V DC for running your 5V projects. At its heart is a TPS61030 boost converter from TI. This boost converter chip has some really nice extras such as low battery detection, 4A internal switch, synchronous conversion, excellent efficiency, and 700KHz high-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
  16 NeoPixel Ring: 16 ultra bright smart LED NeoPixels are arranged in a circle with 1.75" (44.5mm) outer diameter. The rings are 'chainable' - connect the output pin of one to the input pin of another. Use only one microcontroller pin to control as many as you can chain together! Each LED is addressable as the driver chip is inside the LED. Each one has ~18mA constant current drive so the color will be very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
